// Logisim project Mano-Basic-Computer.circ as structural Verilog: 2 circuits, main circuit main
module main (
  input  INC_AR,
  input  CLR_AR,
  input  CLR_PC,
  input  CLR_DR,
  input  INC_AC,
  input  CLR_AC,
  input  CLR_IR,
  input  INC_TR,
  input  CLR_TR
);

  wire and_1_out, and_2_out, and_3_out, and_4_out, and_5_out, and_6_out, and_7_out, and_12_out, and_13_out,
       and_14_out, and_15_out, and_16_out, and_17_out, and_18_out, and_19_out, and_20_out, and_21_out,
       and_22_out, and_23_out, and_24_out, and_25_out, and_26_out, C0, C1, C2, clock_1_out, CLR_SC, D0, D1,
       D2, D3, D4, D5, D6, D7, D8, D9, D10, D11, D12, D13, D14, D15, d_ff_1_q, E, INC_DR, INC_PC, LD_AC,
       LD_AR, LD_DR, LD_E_FF, LD_PC, LD_TR, Memory_Read, Memory_Write, or_1_out, or_2_out, or_3_out,
       or_10_out, or_11_out, or_12_out, or_13_out, or_14_out, or_15_out, or_16_out, or_17_out, Q, S0, S1, S2,
       T0, T1, T2, T3, T4, T5, T6, T7, T8, T9, T10, T11, T12, T13, T14, T15;
  wire [3:0] bit_extender_6_out, SC_q;
  wire [7:0] AR_q, bit_extender_1_out, bit_extender_2_out, bit_extender_7_out, PC_q;
  wire [11:0] bit_extender_5_out, shifter_2_out;
  wire [15:0] AC_q, alu_1_output, bit_extender_3_out, bit_extender_4_out, DR, IR_0_11_In, IR_4_11_Out,
       multiplexer_1_out, ram_1_data, shifter_1_out, TR_q;

  Clock clock_1 (.out(clock_1_out));
  Bit_Extender #(.in_width(16), .out_width(8)) bit_extender_1 (.in(multiplexer_1_out), .out(bit_extender_1_out));
  Bit_Extender #(.in_width(16), .out_width(8)) bit_extender_2 (.in(multiplexer_1_out), .out(bit_extender_2_out));
  ALU alu_1 (.DR(DR), .AC(AC_q), .C2C1C0({C2, C1, C0}), .Output(alu_1_output), .E(E));
  Counter AR (
    .load(LD_AR), .D(bit_extender_1_out), .count(INC_AR), .Q(AR_q), .clk(clock_1_out), .clr(CLR_AR));  // open: carry
  Counter PC (
    .load(LD_PC), .D(bit_extender_2_out), .count(INC_PC), .Q(PC_q), .clk(clock_1_out), .clr(CLR_PC));  // open: carry
  Counter #(.width(16), .max('hffff)) u_DR (
    .load(LD_DR), .D(multiplexer_1_out), .count(INC_DR), .Q(DR), .clk(clock_1_out), .clr(CLR_DR));  // open: carry
  Counter #(.width(16), .max('hffff)) AC (
    .load(LD_AC), .D(alu_1_output), .count(INC_AC), .Q(AC_q), .clk(clock_1_out), .clr(CLR_AC));  // open: carry
  Register #(.width(16)) IR (.D(multiplexer_1_out), .en(T1), .Q(IR_0_11_In), .clk(clock_1_out), .clr(CLR_IR));
  Counter #(.width(16), .max('hffff)) TR (
    .load(LD_TR), .D(multiplexer_1_out), .count(INC_TR), .Q(TR_q), .clk(clock_1_out), .clr(CLR_TR));  // open: carry
  nor nor_1 (Q, DR[0], DR[1], DR[2], DR[3], DR[4], DR[5], DR[6], DR[7], DR[8], DR[9], DR[10], DR[11], DR[12], DR[13], DR[14], DR[15]);
  RAM #(.dataWidth(16), .bus("separate")) ram_1 (
    .addr(AR_q), .din(multiplexer_1_out), .data(ram_1_data), .str(Memory_Write), .clk(clock_1_out),
    .ld(Memory_Read));  // open: sel, clr
  assign bit_extender_3_out = {{8{1'b0}}, AR_q};  // Bit_Extender bit_extender_3
  assign bit_extender_4_out = {{8{1'b0}}, PC_q};  // Bit_Extender bit_extender_4
  D_Flip_Flop E_Flip_Flop (.clk(clock_1_out), .D(E), .en(LD_E_FF));  // open: Q, Qn, preset, reset
  Multiplexer #(.select(3), .width(16), .enable("false")) multiplexer_1 (
    .in1(ram_1_data), .in2(bit_extender_3_out), .in3(bit_extender_4_out), .in4(DR), .in5(AC_q),
    .in6(IR_4_11_Out), .in7(TR_q), .out(multiplexer_1_out), .sel({S2, S1, S0}));  // open: in0
  D_Flip_Flop d_ff_1 (.clk(clock_1_out), .D(CLR_SC), .Q(d_ff_1_q));  // open: Qn, preset, en, reset
  Shifter #(.width(16), .shift("rl")) shifter_1 (.in(IR_0_11_In), .\dist (4'b0100), .out(shifter_1_out));
  Bit_Extender #(.in_width(16), .out_width(12)) bit_extender_5 (.in(IR_0_11_In), .out(bit_extender_5_out));
  Counter #(.width(4), .max('hf)) SC (
    .load(1'b0), .count(1'b1), .Q(SC_q), .clk(clock_1_out), .clr(d_ff_1_q));  // open: D, carry
  Decoder #(.select(4), .enable("false")) decoder_1 (
    .out0(D0), .out1(D1), .out2(D2), .out3(D3), .out4(D4), .out5(D5), .out6(D6), .out7(D7), .out8(D8),
    .out9(D9), .out10(D10), .out11(D11), .out12(D12), .out13(D13), .out14(D14), .out15(D15),
    .sel(bit_extender_6_out));
  Bit_Extender #(.in_width(16), .out_width(4)) bit_extender_6 (.in(shifter_1_out), .out(bit_extender_6_out));
  Decoder #(.select(4)) decoder_2 (
    .out0(T0), .out1(T1), .out2(T2), .out3(T3), .out4(T4), .out5(T5), .out6(T6), .out7(T7), .out8(T8),
    .out9(T9), .out10(T10), .out11(T11), .out12(T12), .out13(T13), .out14(T14), .out15(T15), .sel(SC_q),
    .en(1'b1));
  Shifter #(.width(12), .shift("rr")) shifter_2 (.in(bit_extender_5_out), .\dist (4'b0100), .out(shifter_2_out));
  Bit_Extender #(.in_width(12), .out_width(8)) bit_extender_7 (.in(shifter_2_out), .out(bit_extender_7_out));
  assign IR_4_11_Out = {{8{1'b0}}, bit_extender_7_out};  // Bit_Extender bit_extender_8
  or or_1 (or_1_out, D0, D1, D2, D5, D6);
  or or_2 (or_2_out, T5, T7);
  or or_3 (or_3_out, D0, D1, D2);
  and and_1 (and_1_out, D3, T3);
  and and_2 (and_2_out, D6, T5);
  and and_3 (and_3_out, T3, or_1_out);
  and and_4 (and_4_out, D6, T5, Q);
  and and_5 (and_5_out, D5, T6);
  and and_6 (and_6_out, or_2_out, D5);
  and and_7 (and_7_out, T4, or_3_out);
  or or_4 (Memory_Write, and_1_out, and_2_out);
  or or_5 (Memory_Read, T1, and_3_out);
  or or_6 (LD_DR, and_3_out, and_5_out);
  or or_7 (LD_AR, T0, T2);
  and and_8 (LD_PC, D4, T3);
  or or_8 (INC_PC, T1, and_4_out);
  and and_9 (INC_DR, D6, T4);
  or or_9 (LD_AC, and_6_out, and_7_out);
  and and_10 (LD_E_FF, D1, T4);
  and and_11 (LD_TR, D5, T4);
  or or_10 (or_10_out, D0, D2);
  or or_11 (or_11_out, T5, T7);
  or or_12 (or_12_out, T4, T6);
  or or_13 (or_13_out, T4, T6);
  or or_14 (or_14_out, D0, D1, D2);
  or or_15 (or_15_out, D3, D4);
  or or_16 (or_16_out, D0, D1, D2, D3, D5, D6);
  and and_12 (and_12_out, D5, or_12_out);
  and and_13 (and_13_out, D5, T6);
  and and_14 (and_14_out, D6, T5);
  and and_15 (and_15_out, D5, or_13_out);
  and and_16 (and_16_out, or_14_out, T4);
  and and_17 (and_17_out, T3, or_15_out);
  and and_18 (and_18_out, D5, T7);
  and and_19 (and_19_out, D6, T5);
  and and_20 (and_20_out, T4, or_10_out);
  and and_21 (and_21_out, D5, or_11_out);
  or or_17 (or_17_out, D0, D1);
  and and_22 (and_22_out, D0, T4);
  and and_23 (and_23_out, D5, T7);
  and and_24 (and_24_out, T3, or_16_out);
  and and_25 (and_25_out, T3, D4);
  and and_26 (and_26_out, D3, T3);
  or or_18 (CLR_SC, and_16_out, and_17_out, and_18_out, and_19_out);
  or or_19 (C0, and_20_out, and_21_out);
  and and_27 (C1, T4, or_17_out);
  or or_20 (C2, and_22_out, and_23_out);
  or or_21 (S0, and_24_out, and_12_out, T0, T1);
  or or_22 (S1, and_25_out, and_13_out, T0, T2);
  or or_23 (S2, and_26_out, and_14_out, and_15_out, T2);

  // Other names for the same wires on the sheet: C2C1C0[2:0] = {C2, C1, C0}; IR_12_15_In[15:0] = IR_0_11_In;
  //   S2S1S0[2:0] = {S2, S1, S0}
endmodule

module ALU (
  input  [15:0] DR,
  input  [15:0] AC,
  input  [2:0] C2C1C0,
  output [15:0] Output,
  output E
);

  wire [15:0] adder_1_out, divider_1_out, multiplier_1_out, not_1_out, subtractor_1_out, xor_1_out;

  Divider #(.width(16)) divider_1 (.a(DR), .b(AC), .out(divider_1_out));  // open: upper, rem
  Adder #(.width(16)) adder_1 (.a(DR), .b(AC), .out(adder_1_out), .cout(E));  // open: cin
  Subtractor #(.width(16)) subtractor_1 (.a(DR), .b(AC), .out(subtractor_1_out));  // open: bin, bout
  Multiplier #(.width(16)) multiplier_1 (.a(DR), .b(AC), .out(multiplier_1_out));  // open: cin, cout
  assign not_1_out = ~DR;  // NOT_Gate not_1, 16 bits wide
  assign xor_1_out = DR ^ AC;  // XOR_Gate xor_1, 16 bits wide
  Multiplexer #(.select(3), .width(16), .enable("false")) multiplexer_1 (
    .in1(DR), .in2(adder_1_out), .in3(subtractor_1_out), .in4(multiplier_1_out), .in5(divider_1_out),
    .in6(not_1_out), .in7(xor_1_out), .out(Output), .sel(C2C1C0));  // open: in0
endmodule
